# Fritzing sketch schema (saved by Fritzing 0.5.2b)

parts:
  Arduino1 = Arduino
  R1 = Resistor [resistance=220 package=THT]
  R2 = Resistor [resistance=220 package=THT]
  R3 = Resistor [resistance=220 package=THT]

nets:
  N1: Arduino1.D9, R3.Pin_1
  N2: Arduino1.D8, R2.Pin_1
  N3: Arduino1.D7, R1.Pin_1

notes:
  To video input
